# Fritzing sketch layout (saved by Fritzing 0.9.3b)
breadboards: 1

parts:
  U1 = LM386 [package=dip08]
  IC1 = IC, DIP package, 14 pins [chip_label=CD40106]
  R1 = Photocell (LDR) [package=THT]
  C1 = Ceramic Capacitor [capacitance=100nF package="100 mil [THT, multilayer]"]
  C4 = Ceramic Capacitor [capacitance=100nF package="100 mil [THT, multilayer]"]
  VCC1 = Battery block 9V
  Part1 = Rotary Potentiometer [package=THT]
  C3 = Electrolytic Capacitor [capacitance=47µF package="100 mil [THT, electrolytic]"]
  C5 = Capacitor [package=cap-pth-small2]
  J1 = Piezo Speaker

nets:
  N1: U1.-IN, Part1.wiper, C5.2
  N2: U1.+IN, U1.V-, IC1.pin7, C1.0, C4.1, VCC1.-, Part1.leg2, C5.1, J1.pin2
  N3: U1.OUT, C3.+
  N4: U1.V+, IC1.pin14, C4.0, VCC1.+
  N5: IC1.pin5, R1.pin_0, C1.1
  N6: IC1.pin6, R1.pin_1, Part1.leg1
  N7: C3.-, J1.pin1

custom parts:
  Rotary Potentiometer: Rotary Potentiometer(16mm)
